# Fritzing sketch Schema (saved by Fritzing 0.9.5d)
breadboards: 1

parts:
  U1 = NodeMCU V1.0
  Componente1 = LCD1602-I2C
  Mod1 = KY-009 Full Color RGB LED SMD Module [package="Breakout board"]
  Mod2 = KY-012 Active Buzzer Module [package="Breakout board"]
  Mod3 = KY-018 Photoresistor Module [package="Breakout board"]
  Mod4 = KY-015 Temperature & Humidity Sensor Module [package="Breakout board"]
  R1 = Resistor [tolerance=±5% resistance=200 package=THT]
  R2 = Resistor [tolerance=±5% resistance=200 package=THT]
  LED1 = smd LED [color="Yellow (595nm)" package="0603 [SMD]"]

nets:
  N1: U1.D0, Mod1.G
  N2: U1.D1, Componente1.SCL
  N3: U1.D2, Componente1.SDA
  N4: U1.D3, Mod2.-
  N5: U1.3V3, Mod2.S, Mod3.-, Mod4.S, R1.Pin_0, R1.Pin_1, R2.Pin_0
  GND: U1.GND, Componente1.GND, Mod1.-, Mod3.Vin, Mod4.-
  N6: U1.D5, LED1.cathode
  N7: U1.D6, Mod1.R
  N8: U1.D7, Mod4.Vin
  N9: U1.D8, Mod1.B
  VIN: U1.Vin, Componente1.VCC
  N10: U1.A0, Mod3.S
  N11: R2.Pin_1, LED1.anode

custom parts:
  NodeMCU V1.0: ESP8266 based NodeMCU
  LCD1602-I2C: A standard character display, usually with 2x16 characters. Comes in many colors with LCM1602 IIC attached.
  KY-009 Full Color RGB LED SMD Module: KY-009 RGB full color LED Module, emits a range of colors by mixing red, green and blue light. The amount of each color is adjusted using PWM.
  KY-012 Active Buzzer Module: Active Piezoelectric Buzzer Module KY-012, it produces single-tone sound when signal is high. (Special thanks to vanepp for fixing the PCB holes and other errors)
  KY-018 Photoresistor Module: KY-018 Photoresistor module, used to measure light intensity. It can determine the presence or absence of light.
  KY-015 Temperature & Humidity Sensor Module: KY-015 temperature and humidity sensor module, provides a low-latency serial interface to measure humidity and temperature.
